// Logisim project Controller.circ as structural Verilog: 1 circuit, main circuit Control Store
module Control_Store (
  input  [3:0] in_1,
  output F0,
  output F1,
  output ENA,
  output ENB,
  output INVA,
  output out_7
);

  wire and_1_out, and_2_out, and_3_out, and_4_out, and_5_out, and_6_out, and_7_out, and_8_out, and_9_out,
       and_10_out, and_11_out, not_1_out, not_2_out, not_3_out, not_4_out;

  not not_1 (not_1_out, in_1[3]);
  not not_2 (not_2_out, in_1[2]);
  not not_3 (not_3_out, in_1[1]);
  not not_4 (not_4_out, in_1[0]);
  and and_1 (and_1_out, not_1_out, not_2_out);
  and and_2 (and_2_out, not_2_out, in_1[0]);
  or or_1 (F0, and_1_out, and_2_out, and_3_out);
  and and_3 (and_3_out, in_1[1], not_4_out);
  or or_2 (F1, not_2_out, in_1[1], in_1[0]);
  or or_3 (ENA, in_1[3], in_1[2], in_1[1], not_4_out);
  and and_4 (and_4_out, not_1_out, not_3_out, in_1[0]);
  and and_5 (and_5_out, in_1[2], not_3_out);
  or or_4 (ENB, and_4_out, and_5_out, and_6_out);
  and and_6 (and_6_out, not_2_out, in_1[1]);
  and and_7 (and_7_out, not_2_out, in_1[0]);
  or or_5 (INVA, and_7_out, and_8_out);
  and and_8 (and_8_out, in_1[3], not_2_out, not_3_out);
  and and_9 (and_9_out, not_1_out, not_2_out, in_1[1], not_4_out);
  and and_10 (and_10_out, not_2_out, in_1[1], in_1[0]);
  or or_6 (out_7, and_9_out, and_10_out, and_11_out);
  and and_11 (and_11_out, in_1[3], not_2_out, in_1[0]);

  // Notes on the sheet:
  //   A
  //   B
  //   C
  //   D
  //   INC
endmodule
